// Logisim project ReactionGame.circ as structural Verilog: 1 circuit, main circuit main
module main (
);

  wire and_1_out, and_2_out, and_3_out, and_4_out, and_5_out, and_6_out, and_7_out, clock_1_out, d_ff_1_q,
       d_ff_1_qn, d_ff_2_q, d_ff_2_qn, d_ff_3_q, d_ff_3_qn, L_out, nand_1_out, nand_2_out, nand_3_out,
       nand_4_out, nand_5_out, nand_6_out, not_1_out, not_2_out, not_3_out, not_4_out, or_1_out, or_2_out,
       or_3_out, or_4_out, or_5_out, P1_out, P2_out, R_out;

  Button L (.out(L_out));
  Button P1 (.out(P1_out));
  Button R (.out(R_out));
  not not_1 (not_1_out, R_out);
  Button P2 (.out(P2_out));
  not not_2 (not_2_out, or_1_out);
  or or_1 (or_1_out, or_2_out, d_ff_1_q);
  not not_3 (not_3_out, or_2_out);
  not not_4 (not_4_out, or_2_out);
  or or_2 (or_2_out, d_ff_3_q, d_ff_2_q);
  and and_1 (and_1_out, L_out, not_2_out, not_1_out);
  and and_2 (and_2_out, or_1_out, d_ff_1_q, not_1_out);
  and and_3 (and_3_out, P1_out, not_3_out, not_1_out);
  and and_4 (and_4_out, or_2_out, d_ff_2_q, not_1_out);
  and and_5 (and_5_out, P2_out, not_4_out, not_1_out);
  and and_6 (and_6_out, or_2_out, d_ff_3_q, not_1_out);
  or or_3 (or_3_out, and_1_out, and_2_out);
  or or_4 (or_4_out, and_3_out, and_4_out);
  or or_5 (or_5_out, and_5_out, and_6_out);
  Clock clock_1 (.out(clock_1_out));
  D_Flip_Flop d_ff_1 (.clk(clock_1_out), .D(or_3_out), .Q(d_ff_1_q), .Qn(d_ff_1_qn));  // open: preset, en, reset
  D_Flip_Flop d_ff_2 (.clk(clock_1_out), .D(or_4_out), .Q(d_ff_2_q), .Qn(d_ff_2_qn));  // open: preset, en, reset
  D_Flip_Flop d_ff_3 (.clk(clock_1_out), .D(or_5_out), .Q(d_ff_3_q), .Qn(d_ff_3_qn));  // open: preset, en, reset
  nand nand_1 (nand_1_out, d_ff_2_qn, d_ff_1_qn, d_ff_3_q);
  nand nand_2 (nand_2_out, d_ff_2_q, d_ff_1_q, d_ff_3_qn);
  nand nand_3 (nand_3_out, d_ff_2_q, d_ff_1_qn, d_ff_3_qn);
  nand nand_4 (nand_4_out, d_ff_2_qn, d_ff_1_q, d_ff_3_q);
  nand nand_5 (nand_5_out, nand_1_out, nand_2_out);
  and and_7 (and_7_out, d_ff_2_q, d_ff_3_q);
  nand nand_6 (nand_6_out, nand_3_out, nand_4_out);
  LED P1_WINS (.in(nand_5_out));
  LED TIE (.in(and_7_out));
  LED P2_WINS (.in(nand_6_out));
  LED LIGHT (.in(d_ff_1_q));

  // Notes on the sheet:
  //   P2  P1  L
endmodule
